// Logisim project hw4.circ as structural Verilog: 10 circuits, main circuit main
module main (
  input  reset
);

  wire ALU_immed, and_1_out, and_2_out, and_3_out, blt, bne, clk, \input , keyboard_1_avail, load, neg_flag,
       nonzero_flag, not_1_out, not_2_out, or_1_out, \output , Rd_is_Rt, shift, shift_right, store, write_en;
  wire [1:0] ALU_op, jump;
  wire [2:0] multiplexer_4_out, multiplexer_5_out, Rd, Rs_instr, Rt, shamt;
  wire [5:0] immed_instr;
  wire [6:0] keyboard_1_data;
  wire [7:7] not_3_out;
  wire [11:0] addr;
  wire [15:0] alu_2_out, alu_3_out, immed, multiplexer_2_out, multiplexer_3_out, multiplexer_6_out,
       multiplexer_7_out, multiplexer_8_out, new_PC, PC, PC_1, ram_1_data, registerfile_1_rt_val, rom_1_data,
       Rs, shifter_1_out, to_reg_file;

  not not_1 (not_1_out, clk);
  _16_bit_register u_PC (.D(multiplexer_2_out), .clk(not_1_out), .en(1'b1), .reset(reset), .Q(PC));
  ALU alu_1 (.in1(16'h1), .in2(PC), .op(2'b00), .out(PC_1));  // open: not_zero, neg
  ROM #(.addrWidth(16), .dataWidth(16)) rom_1 (.addr(PC), .data(rom_1_data));  // open: sel
  ALU alu_2 (.in1(PC_1), .in2(immed), .op(2'b00), .out(alu_2_out));  // open: not_zero, neg
  and and_1 (and_1_out, nonzero_flag, bne);
  Multiplexer #(.width(16), .enable("false")) multiplexer_1 (.in0(PC_1), .in1(alu_2_out), .out(new_PC), .sel(or_1_out));
  or or_1 (or_1_out, and_1_out, and_2_out);
  and and_2 (and_2_out, neg_flag, blt);
  control control_1 (
    .instruction(rom_1_data), .Rd_is_Rt(Rd_is_Rt), .ALU_op(ALU_op), .write_en(write_en),
    .ALU_immed(ALU_immed), .shift(shift), .shift_right(shift_right), .load(load), .store(store), .bne(bne),
    .blt(blt), .jump(jump), .\input (\input ), .\output (\output ), .addr(addr), .immed(immed_instr),
    .shamt(shamt), .Rd(Rd), .Rt(Rt), .Rs(Rs_instr));
  Multiplexer #(.select(2), .width(16), .enable("false")) multiplexer_2 (
    .in0(new_PC), .in1({PC[15:12], addr}), .in2(Rs), .in3({PC[15:12], addr}), .out(multiplexer_2_out),
    .sel(jump));
  and and_3 (and_3_out, jump[0], jump[1]);
  Clock clock_1 (.out(clk));
  RegisterFile registerfile_1 (
    .Rd_val(multiplexer_3_out), .clk(clk), .en(write_en), .reset(reset), .Rd(multiplexer_4_out),
    .Rs(Rs_instr), .Rt(Rt), .Rs_val(Rs), .Rt_val(registerfile_1_rt_val));
  Multiplexer #(.width(16), .enable("false")) multiplexer_3 (
    .in0(to_reg_file), .in1(PC_1), .out(multiplexer_3_out), .sel(and_3_out));
  Multiplexer #(.width(3), .enable("false")) multiplexer_4 (
    .in0(multiplexer_5_out), .in1(3'b111), .out(multiplexer_4_out), .sel(and_3_out));
  Multiplexer #(.width(3), .enable("false")) multiplexer_5 (
    .in0(Rd), .in1(Rt), .out(multiplexer_5_out), .sel(Rd_is_Rt));
  TTY #(.rows(13), .cols(80), .trigger("falling")) tty_1 (.data(Rs[6:0]), .clk(clk), .we(\output ), .clr(reset));
  shifter shifter_1 (.in(Rs), .shamt(shamt), .l_or_r(shift_right), .out(shifter_1_out));
  sign_extend sign_extend_1 (.in(immed_instr), .out(immed));
  Multiplexer #(.width(16), .enable("false")) multiplexer_6 (
    .in0(registerfile_1_rt_val), .in1(immed), .out(multiplexer_6_out), .sel(ALU_immed));
  ALU alu_3 (.in1(Rs), .in2(multiplexer_6_out), .op(ALU_op), .out(alu_3_out), .not_zero(nonzero_flag), .neg(neg_flag));
  not not_2 (not_2_out, shift);
  Multiplexer #(.width(16), .enable("false")) multiplexer_7 (
    .in0(shifter_1_out), .in1(alu_3_out), .out(multiplexer_7_out), .sel(not_2_out));
  Keyboard keyboard_1 (.clk(clk), .re(\input ), .clr(reset), .avail(keyboard_1_avail), .data(keyboard_1_data));
  RAM #(.addrWidth(16), .dataWidth(16), .bus("separate")) ram_1 (
    .addr(multiplexer_7_out), .din(registerfile_1_rt_val), .data(ram_1_data), .str(store), .clk(clk));  // open: sel, ld, clr
  Multiplexer #(.width(16), .enable("false")) multiplexer_8 (
    .in0(multiplexer_7_out), .in1(ram_1_data), .out(multiplexer_8_out), .sel(load));
  not not_3 (not_3_out[7], keyboard_1_avail);
  Multiplexer #(.width(16), .enable("false")) multiplexer_9 (
    .in0(multiplexer_8_out), .in1({{8{1'b0}}, not_3_out[7], keyboard_1_data}), .out(to_reg_file),
    .sel(\input ));

  // Notes on the sheet:
  //   Branch or increment circuitry
endmodule

module ALU (
  input  [15:0] in1,
  input  [15:0] in2,
  input  [1:0] op,
  output [15:0] out,
  output not_zero,
  output neg
);

  wire and_1_out, n1_bit_adder_1_cout, n1_bit_adder_2_cout, n1_bit_adder_3_cout, n1_bit_adder_4_cout,
       n1_bit_adder_5_cout, n1_bit_adder_6_cout, n1_bit_adder_7_cout, n1_bit_adder_8_cout,
       n1_bit_adder_9_cout, n1_bit_adder_10_cout, n1_bit_adder_11_cout, n1_bit_adder_12_cout,
       n1_bit_adder_13_cout, n1_bit_adder_14_cout, n1_bit_adder_15_cout, not_2_out;
  wire [15:0] multiplexer_1_out, not_1_out, not_3_out, sum, xor_1_out;

  assign not_1_out = ~in2;  // NOT_Gate not_1, 16 bits wide
  Multiplexer #(.width(16), .enable("false")) multiplexer_1 (
    .in0(in2), .in1(not_1_out), .out(multiplexer_1_out), .sel(and_1_out));
  and and_1 (and_1_out, not_2_out, op[0]);
  not not_2 (not_2_out, op[1]);
  _1_bit_adder u_1_bit_adder_1 (
    .in1(multiplexer_1_out[0]), .in2(in1[0]), .cin(and_1_out), .cout(n1_bit_adder_1_cout), .out(sum[0]));
  _1_bit_adder u_1_bit_adder_2 (
    .in1(multiplexer_1_out[1]), .in2(in1[1]), .cin(n1_bit_adder_1_cout), .cout(n1_bit_adder_2_cout),
    .out(sum[1]));
  _1_bit_adder u_1_bit_adder_3 (
    .in1(multiplexer_1_out[2]), .in2(in1[2]), .cin(n1_bit_adder_2_cout), .cout(n1_bit_adder_3_cout),
    .out(sum[2]));
  _1_bit_adder u_1_bit_adder_4 (
    .in1(multiplexer_1_out[3]), .in2(in1[3]), .cin(n1_bit_adder_3_cout), .cout(n1_bit_adder_4_cout),
    .out(sum[3]));
  _1_bit_adder u_1_bit_adder_5 (
    .in1(multiplexer_1_out[4]), .in2(in1[4]), .cin(n1_bit_adder_4_cout), .cout(n1_bit_adder_5_cout),
    .out(sum[4]));
  _1_bit_adder u_1_bit_adder_6 (
    .in1(multiplexer_1_out[5]), .in2(in1[5]), .cin(n1_bit_adder_5_cout), .cout(n1_bit_adder_6_cout),
    .out(sum[5]));
  _1_bit_adder u_1_bit_adder_7 (
    .in1(multiplexer_1_out[6]), .in2(in1[6]), .cin(n1_bit_adder_6_cout), .cout(n1_bit_adder_7_cout),
    .out(sum[6]));
  _1_bit_adder u_1_bit_adder_8 (
    .in1(multiplexer_1_out[7]), .in2(in1[7]), .cin(n1_bit_adder_7_cout), .cout(n1_bit_adder_8_cout),
    .out(sum[7]));
  _1_bit_adder u_1_bit_adder_9 (
    .in1(multiplexer_1_out[8]), .in2(in1[8]), .cin(n1_bit_adder_8_cout), .cout(n1_bit_adder_9_cout),
    .out(sum[8]));
  _1_bit_adder u_1_bit_adder_10 (
    .in1(multiplexer_1_out[9]), .in2(in1[9]), .cin(n1_bit_adder_9_cout), .cout(n1_bit_adder_10_cout),
    .out(sum[9]));
  _1_bit_adder u_1_bit_adder_11 (
    .in1(multiplexer_1_out[10]), .in2(in1[10]), .cin(n1_bit_adder_10_cout), .cout(n1_bit_adder_11_cout),
    .out(sum[10]));
  _1_bit_adder u_1_bit_adder_12 (
    .in1(multiplexer_1_out[11]), .in2(in1[11]), .cin(n1_bit_adder_11_cout), .cout(n1_bit_adder_12_cout),
    .out(sum[11]));
  _1_bit_adder u_1_bit_adder_13 (
    .in1(multiplexer_1_out[12]), .in2(in1[12]), .cin(n1_bit_adder_12_cout), .cout(n1_bit_adder_13_cout),
    .out(sum[12]));
  _1_bit_adder u_1_bit_adder_14 (
    .in1(multiplexer_1_out[13]), .in2(in1[13]), .cin(n1_bit_adder_13_cout), .cout(n1_bit_adder_14_cout),
    .out(sum[13]));
  _1_bit_adder u_1_bit_adder_15 (
    .in1(multiplexer_1_out[14]), .in2(in1[14]), .cin(n1_bit_adder_14_cout), .cout(n1_bit_adder_15_cout),
    .out(sum[14]));
  _1_bit_adder u_1_bit_adder_16 (
    .in1(multiplexer_1_out[15]), .in2(in1[15]), .cin(n1_bit_adder_15_cout), .out(sum[15]));  // open: cout
  assign not_3_out = ~in1;  // NOT_Gate not_3, 16 bits wide
  assign xor_1_out = in1 ^ in2;  // XOR_Gate xor_1, 16 bits wide
  Multiplexer #(.select(2), .width(16), .enable("false")) multiplexer_2 (
    .in0(sum), .in1(sum), .in2(not_3_out), .in3(xor_1_out), .out({neg, out[14:0]}), .sel(op));
  or or_1 (not_zero, out[0], out[1], out[2], out[3], out[4], out[5], out[6], out[7], out[8], out[9], out[10], out[11], out[12], out[13], out[14], neg);

  assign out[15] = neg;
endmodule

// +
module _1_bit_adder (
  input  cin,
  input  in1,
  input  in2,
  output out,
  output cout
);

  wire and_1_out, and_2_out, xor_1_out;

  and and_1 (and_1_out, cin, in1);
  xor xor_1 (xor_1_out, cin, in1);
  xor xor_2 (out, xor_1_out, in2);
  and and_2 (and_2_out, xor_1_out, in2);
  or or_1 (cout, and_2_out, and_1_out);
endmodule

// reg
module _16_bit_register (
  input  [15:0] D,
  input  clk,
  input  en,
  input  reset,
  output [15:0] Q
);

  D_Flip_Flop #(.trigger("falling")) d_ff_1 (
    .clk(clk), .D(D[0]), .Q(Q[0]), .en(en), .reset(reset));  // open: Qn, preset
  D_Flip_Flop #(.trigger("falling")) d_ff_2 (
    .clk(clk), .D(D[1]), .Q(Q[1]), .en(en), .reset(reset));  // open: Qn, preset
  D_Flip_Flop #(.trigger("falling")) d_ff_3 (
    .clk(clk), .D(D[2]), .Q(Q[2]), .en(en), .reset(reset));  // open: Qn, preset
  D_Flip_Flop #(.trigger("falling")) d_ff_4 (
    .clk(clk), .D(D[3]), .Q(Q[3]), .en(en), .reset(reset));  // open: Qn, preset
  D_Flip_Flop #(.trigger("falling")) d_ff_5 (
    .clk(clk), .D(D[4]), .Q(Q[4]), .en(en), .reset(reset));  // open: Qn, preset
  D_Flip_Flop #(.trigger("falling")) d_ff_6 (
    .clk(clk), .D(D[5]), .Q(Q[5]), .en(en), .reset(reset));  // open: Qn, preset
  D_Flip_Flop #(.trigger("falling")) d_ff_7 (
    .clk(clk), .D(D[6]), .Q(Q[6]), .en(en), .reset(reset));  // open: Qn, preset
  D_Flip_Flop #(.trigger("falling")) d_ff_8 (
    .clk(clk), .D(D[7]), .Q(Q[7]), .en(en), .reset(reset));  // open: Qn, preset
  D_Flip_Flop #(.trigger("falling")) d_ff_9 (
    .clk(clk), .D(D[8]), .Q(Q[8]), .en(en), .reset(reset));  // open: Qn, preset
  D_Flip_Flop #(.trigger("falling")) d_ff_10 (
    .clk(clk), .D(D[9]), .Q(Q[9]), .en(en), .reset(reset));  // open: Qn, preset
  D_Flip_Flop #(.trigger("falling")) d_ff_11 (
    .clk(clk), .D(D[10]), .Q(Q[10]), .en(en), .reset(reset));  // open: Qn, preset
  D_Flip_Flop #(.trigger("falling")) d_ff_12 (
    .clk(clk), .D(D[11]), .Q(Q[11]), .en(en), .reset(reset));  // open: Qn, preset
  D_Flip_Flop #(.trigger("falling")) d_ff_13 (
    .clk(clk), .D(D[12]), .Q(Q[12]), .en(en), .reset(reset));  // open: Qn, preset
  D_Flip_Flop #(.trigger("falling")) d_ff_14 (
    .clk(clk), .D(D[13]), .Q(Q[13]), .en(en), .reset(reset));  // open: Qn, preset
  D_Flip_Flop #(.trigger("falling")) d_ff_15 (
    .clk(clk), .D(D[14]), .Q(Q[14]), .en(en), .reset(reset));  // open: Qn, preset
  D_Flip_Flop #(.trigger("falling")) d_ff_16 (
    .clk(clk), .D(D[15]), .Q(Q[15]), .en(en), .reset(reset));  // open: Qn, preset
endmodule

// reg file
module RegisterFile (
  input  clk,
  input  en,
  input  reset,
  input  [15:0] Rd_val,
  input  [2:0] Rd,
  input  [2:0] Rt,
  input  [2:0] Rs,
  output [15:0] Rs_val,
  output [15:0] Rt_val
);

  wire and_1_out, and_2_out, and_3_out, and_4_out, and_5_out, and_6_out, and_7_out, decoder_2_out0,
       decoder_2_out1, decoder_2_out2, decoder_2_out3, decoder_2_out4, decoder_2_out5, decoder_2_out6,
       decoder_2_out7, decoder_3_out0, decoder_3_out1, decoder_3_out2, decoder_3_out3, decoder_3_out4,
       decoder_3_out5, decoder_3_out6, decoder_3_out7, en1, en2, en3, en4, en5, en6, en7;
  wire [15:0] n16_bit_register_8_q, r0, r1, r2, r3, r4, r5, r6;

  Decoder #(.select(3), .enable("false")) decoder_1 (
    .out1(en1), .out2(en2), .out3(en3), .out4(en4), .out5(en5), .out6(en6), .out7(en7), .sel(Rd));  // open: out0
  // Probe on r0
  // Probe on r1
  // Probe on r2
  // Probe on r3
  // Probe on r4
  // Probe on r5
  // Probe on r6
  _16_bit_register u_16_bit_register_1 (.D(Rd_val), .clk(clk), .en(1'b0), .reset(reset), .Q(r0));
  and and_1 (and_1_out, en, en1);
  _16_bit_register u_16_bit_register_2 (.D(Rd_val), .clk(clk), .en(and_1_out), .reset(reset), .Q(r1));
  and and_2 (and_2_out, en, en2);
  _16_bit_register u_16_bit_register_3 (.D(Rd_val), .clk(clk), .en(and_2_out), .reset(reset), .Q(r2));
  and and_3 (and_3_out, en, en3);
  _16_bit_register u_16_bit_register_4 (.D(Rd_val), .clk(clk), .en(and_3_out), .reset(reset), .Q(r3));
  and and_4 (and_4_out, en, en4);
  _16_bit_register u_16_bit_register_5 (.D(Rd_val), .clk(clk), .en(and_4_out), .reset(reset), .Q(r4));
  and and_5 (and_5_out, en, en5);
  _16_bit_register u_16_bit_register_6 (.D(Rd_val), .clk(clk), .en(and_5_out), .reset(reset), .Q(r5));
  and and_6 (and_6_out, en, en6);
  _16_bit_register u_16_bit_register_7 (.D(Rd_val), .clk(clk), .en(and_6_out), .reset(reset), .Q(r6));
  and and_7 (and_7_out, en, en7);
  _16_bit_register u_16_bit_register_8 (.D(Rd_val), .clk(clk), .en(and_7_out), .reset(reset), .Q(n16_bit_register_8_q));
  // Probe on n16_bit_register_8_q
  assign Rs_val = decoder_2_out0 ? r0 : 16'bz;  // Controlled_Buffer controlled_buffer_1
  Decoder #(.select(3), .enable("false")) decoder_2 (
    .out0(decoder_2_out0), .out1(decoder_2_out1), .out2(decoder_2_out2), .out3(decoder_2_out3),
    .out4(decoder_2_out4), .out5(decoder_2_out5), .out6(decoder_2_out6), .out7(decoder_2_out7), .sel(Rs));
  assign Rs_val = decoder_2_out1 ? r1 : 16'bz;  // Controlled_Buffer controlled_buffer_2
  assign Rs_val = decoder_2_out2 ? r2 : 16'bz;  // Controlled_Buffer controlled_buffer_3
  assign Rs_val = decoder_2_out3 ? r3 : 16'bz;  // Controlled_Buffer controlled_buffer_4
  assign Rs_val = decoder_2_out4 ? r4 : 16'bz;  // Controlled_Buffer controlled_buffer_5
  assign Rs_val = decoder_2_out5 ? r5 : 16'bz;  // Controlled_Buffer controlled_buffer_6
  assign Rs_val = decoder_2_out6 ? r6 : 16'bz;  // Controlled_Buffer controlled_buffer_7
  assign Rs_val = decoder_2_out7 ? n16_bit_register_8_q : 16'bz;  // Controlled_Buffer controlled_buffer_8
  assign Rt_val = decoder_3_out0 ? r0 : 16'bz;  // Controlled_Buffer controlled_buffer_9
  Decoder #(.select(3), .enable("false")) decoder_3 (
    .out0(decoder_3_out0), .out1(decoder_3_out1), .out2(decoder_3_out2), .out3(decoder_3_out3),
    .out4(decoder_3_out4), .out5(decoder_3_out5), .out6(decoder_3_out6), .out7(decoder_3_out7), .sel(Rt));
  assign Rt_val = decoder_3_out1 ? r1 : 16'bz;  // Controlled_Buffer controlled_buffer_10
  assign Rt_val = decoder_3_out2 ? r2 : 16'bz;  // Controlled_Buffer controlled_buffer_11
  assign Rt_val = decoder_3_out3 ? r3 : 16'bz;  // Controlled_Buffer controlled_buffer_12
  assign Rt_val = decoder_3_out4 ? r4 : 16'bz;  // Controlled_Buffer controlled_buffer_13
  assign Rt_val = decoder_3_out5 ? r5 : 16'bz;  // Controlled_Buffer controlled_buffer_14
  assign Rt_val = decoder_3_out6 ? r6 : 16'bz;  // Controlled_Buffer controlled_buffer_15
  assign Rt_val = decoder_3_out7 ? n16_bit_register_8_q : 16'bz;  // Controlled_Buffer controlled_buffer_16
endmodule

// sign\next
module sign_extend (
  input  [5:0] in,
  output [15:0] out
);


  assign out = {{11{in[5]}}, in[4:0]};
endmodule

// sll
module shift_left (
  input  [2:0] shamt,
  input  [15:0] in,
  output [15:0] out
);

  wire multiplexer_1_out, multiplexer_2_out, multiplexer_3_out, multiplexer_4_out, multiplexer_5_out,
       multiplexer_6_out, multiplexer_7_out, multiplexer_8_out, multiplexer_9_out, multiplexer_10_out,
       multiplexer_11_out, multiplexer_12_out, multiplexer_13_out, multiplexer_14_out, multiplexer_15_out,
       multiplexer_16_out, multiplexer_17_out, multiplexer_18_out, multiplexer_19_out, multiplexer_20_out,
       multiplexer_21_out, multiplexer_22_out, multiplexer_23_out, multiplexer_24_out, multiplexer_26_out,
       multiplexer_27_out, multiplexer_28_out, multiplexer_31_out, multiplexer_32_out, multiplexer_33_out,
       multiplexer_37_out, multiplexer_38_out, shamt0, shamt1, shamt2;

  Multiplexer #(.enable("false")) multiplexer_1 (.in0(1'b0), .in1(in[0]), .out(multiplexer_1_out), .sel(shamt0));
  Multiplexer #(.enable("false")) multiplexer_2 (.in0(in[0]), .in1(in[1]), .out(multiplexer_2_out), .sel(shamt0));
  Multiplexer #(.enable("false")) multiplexer_3 (.in0(in[1]), .in1(in[2]), .out(multiplexer_3_out), .sel(shamt0));
  Multiplexer #(.enable("false")) multiplexer_4 (.in0(in[2]), .in1(in[3]), .out(multiplexer_4_out), .sel(shamt0));
  Multiplexer #(.enable("false")) multiplexer_5 (.in0(in[3]), .in1(in[4]), .out(multiplexer_5_out), .sel(shamt0));
  Multiplexer #(.enable("false")) multiplexer_6 (.in0(in[4]), .in1(in[5]), .out(multiplexer_6_out), .sel(shamt0));
  assign {shamt2, shamt1, shamt0} = ~shamt;  // NOT_Gate not_1, 3 bits wide
  Multiplexer #(.enable("false")) multiplexer_7 (.in0(in[5]), .in1(in[6]), .out(multiplexer_7_out), .sel(shamt0));
  Multiplexer #(.enable("false")) multiplexer_8 (.in0(in[6]), .in1(in[7]), .out(multiplexer_8_out), .sel(shamt0));
  Multiplexer #(.enable("false")) multiplexer_9 (.in0(in[7]), .in1(in[8]), .out(multiplexer_9_out), .sel(shamt0));
  Multiplexer #(.enable("false")) multiplexer_10 (
    .in0(1'b0), .in1(multiplexer_1_out), .out(multiplexer_10_out), .sel(shamt1));
  Multiplexer #(.enable("false")) multiplexer_11 (
    .in0(1'b0), .in1(multiplexer_2_out), .out(multiplexer_11_out), .sel(shamt1));
  Multiplexer #(.enable("false")) multiplexer_12 (
    .in0(multiplexer_1_out), .in1(multiplexer_3_out), .out(multiplexer_12_out), .sel(shamt1));
  Multiplexer #(.enable("false")) multiplexer_13 (.in0(in[8]), .in1(in[9]), .out(multiplexer_13_out), .sel(shamt0));
  Multiplexer #(.enable("false")) multiplexer_14 (.in0(in[9]), .in1(in[10]), .out(multiplexer_14_out), .sel(shamt0));
  Multiplexer #(.enable("false")) multiplexer_15 (.in0(in[10]), .in1(in[11]), .out(multiplexer_15_out), .sel(shamt0));
  Multiplexer #(.enable("false")) multiplexer_16 (
    .in0(multiplexer_2_out), .in1(multiplexer_4_out), .out(multiplexer_16_out), .sel(shamt1));
  Multiplexer #(.enable("false")) multiplexer_17 (
    .in0(multiplexer_3_out), .in1(multiplexer_5_out), .out(multiplexer_17_out), .sel(shamt1));
  Multiplexer #(.enable("false")) multiplexer_18 (
    .in0(multiplexer_4_out), .in1(multiplexer_6_out), .out(multiplexer_18_out), .sel(shamt1));
  Multiplexer #(.enable("false")) multiplexer_19 (.in0(in[11]), .in1(in[12]), .out(multiplexer_19_out), .sel(shamt0));
  Multiplexer #(.enable("false")) multiplexer_20 (.in0(in[12]), .in1(in[13]), .out(multiplexer_20_out), .sel(shamt0));
  Multiplexer #(.enable("false")) multiplexer_21 (
    .in0(multiplexer_5_out), .in1(multiplexer_7_out), .out(multiplexer_21_out), .sel(shamt1));
  Multiplexer #(.enable("false")) multiplexer_22 (
    .in0(multiplexer_6_out), .in1(multiplexer_8_out), .out(multiplexer_22_out), .sel(shamt1));
  Multiplexer #(.enable("false")) multiplexer_23 (.in0(in[13]), .in1(in[14]), .out(multiplexer_23_out), .sel(shamt0));
  Multiplexer #(.enable("false")) multiplexer_24 (.in0(in[14]), .in1(in[15]), .out(multiplexer_24_out), .sel(shamt0));
  Multiplexer #(.enable("false")) multiplexer_25 (.in0(1'b0), .in1(multiplexer_10_out), .out(out[0]), .sel(shamt2));
  Multiplexer #(.enable("false")) multiplexer_26 (
    .in0(multiplexer_7_out), .in1(multiplexer_9_out), .out(multiplexer_26_out), .sel(shamt1));
  Multiplexer #(.enable("false")) multiplexer_27 (
    .in0(multiplexer_8_out), .in1(multiplexer_13_out), .out(multiplexer_27_out), .sel(shamt1));
  Multiplexer #(.enable("false")) multiplexer_28 (
    .in0(multiplexer_9_out), .in1(multiplexer_14_out), .out(multiplexer_28_out), .sel(shamt1));
  Multiplexer #(.enable("false")) multiplexer_29 (.in0(1'b0), .in1(multiplexer_11_out), .out(out[1]), .sel(shamt2));
  Multiplexer #(.enable("false")) multiplexer_30 (.in0(1'b0), .in1(multiplexer_12_out), .out(out[2]), .sel(shamt2));
  Multiplexer #(.enable("false")) multiplexer_31 (
    .in0(multiplexer_13_out), .in1(multiplexer_15_out), .out(multiplexer_31_out), .sel(shamt1));
  Multiplexer #(.enable("false")) multiplexer_32 (
    .in0(multiplexer_14_out), .in1(multiplexer_19_out), .out(multiplexer_32_out), .sel(shamt1));
  Multiplexer #(.enable("false")) multiplexer_33 (
    .in0(multiplexer_15_out), .in1(multiplexer_20_out), .out(multiplexer_33_out), .sel(shamt1));
  Multiplexer #(.enable("false")) multiplexer_34 (.in0(1'b0), .in1(multiplexer_16_out), .out(out[3]), .sel(shamt2));
  Multiplexer #(.enable("false")) multiplexer_35 (
    .in0(multiplexer_10_out), .in1(multiplexer_17_out), .out(out[4]), .sel(shamt2));
  Multiplexer #(.enable("false")) multiplexer_36 (
    .in0(multiplexer_11_out), .in1(multiplexer_18_out), .out(out[5]), .sel(shamt2));
  Multiplexer #(.enable("false")) multiplexer_37 (
    .in0(multiplexer_19_out), .in1(multiplexer_23_out), .out(multiplexer_37_out), .sel(shamt1));
  Multiplexer #(.enable("false")) multiplexer_38 (
    .in0(multiplexer_20_out), .in1(multiplexer_24_out), .out(multiplexer_38_out), .sel(shamt1));
  Multiplexer #(.enable("false")) multiplexer_39 (
    .in0(multiplexer_12_out), .in1(multiplexer_21_out), .out(out[6]), .sel(shamt2));
  Multiplexer #(.enable("false")) multiplexer_40 (
    .in0(multiplexer_16_out), .in1(multiplexer_22_out), .out(out[7]), .sel(shamt2));
  Multiplexer #(.enable("false")) multiplexer_41 (
    .in0(multiplexer_17_out), .in1(multiplexer_26_out), .out(out[8]), .sel(shamt2));
  Multiplexer #(.enable("false")) multiplexer_42 (
    .in0(multiplexer_18_out), .in1(multiplexer_27_out), .out(out[9]), .sel(shamt2));
  Multiplexer #(.enable("false")) multiplexer_43 (
    .in0(multiplexer_21_out), .in1(multiplexer_28_out), .out(out[10]), .sel(shamt2));
  Multiplexer #(.enable("false")) multiplexer_44 (
    .in0(multiplexer_22_out), .in1(multiplexer_31_out), .out(out[11]), .sel(shamt2));
  Multiplexer #(.enable("false")) multiplexer_45 (
    .in0(multiplexer_26_out), .in1(multiplexer_32_out), .out(out[12]), .sel(shamt2));
  Multiplexer #(.enable("false")) multiplexer_46 (
    .in0(multiplexer_27_out), .in1(multiplexer_33_out), .out(out[13]), .sel(shamt2));
  Multiplexer #(.enable("false")) multiplexer_47 (
    .in0(multiplexer_28_out), .in1(multiplexer_37_out), .out(out[14]), .sel(shamt2));
  Multiplexer #(.enable("false")) multiplexer_48 (
    .in0(multiplexer_31_out), .in1(multiplexer_38_out), .out(out[15]), .sel(shamt2));
endmodule

// shift
module shifter (
  input  [2:0] shamt,
  input  l_or_r,
  input  [15:0] in,
  output [15:0] out
);

  wire [15:0] shift_left_1_out, shift_right_1_out;

  shift_left shift_left_1 (.in(in), .shamt(shamt), .out(shift_left_1_out));
  shift_right shift_right_1 (.in(in), .shamt(shamt), .out(shift_right_1_out));
  Multiplexer #(.width(16), .enable("false")) multiplexer_1 (
    .in0(shift_left_1_out), .in1(shift_right_1_out), .out(out), .sel(l_or_r));
endmodule

// srl
module shift_right (
  input  [2:0] shamt,
  input  [15:0] in,
  output [15:0] out
);

  wire multiplexer_1_out, multiplexer_2_out, multiplexer_3_out, multiplexer_4_out, multiplexer_5_out,
       multiplexer_6_out, multiplexer_7_out, multiplexer_8_out, multiplexer_9_out, multiplexer_10_out,
       multiplexer_11_out, multiplexer_12_out, multiplexer_13_out, multiplexer_14_out, multiplexer_15_out,
       multiplexer_16_out, multiplexer_17_out, multiplexer_18_out, multiplexer_19_out, multiplexer_20_out,
       multiplexer_21_out, multiplexer_22_out, multiplexer_23_out, multiplexer_24_out, multiplexer_25_out,
       multiplexer_27_out, multiplexer_28_out, multiplexer_29_out, multiplexer_32_out, multiplexer_33_out,
       multiplexer_34_out, multiplexer_38_out;

  Multiplexer #(.enable("false")) multiplexer_1 (.in0(in[0]), .in1(in[1]), .out(multiplexer_1_out), .sel(shamt[0]));
  Multiplexer #(.enable("false")) multiplexer_2 (.in0(in[1]), .in1(in[2]), .out(multiplexer_2_out), .sel(shamt[0]));
  Multiplexer #(.enable("false")) multiplexer_3 (.in0(in[2]), .in1(in[3]), .out(multiplexer_3_out), .sel(shamt[0]));
  Multiplexer #(.enable("false")) multiplexer_4 (.in0(in[3]), .in1(in[4]), .out(multiplexer_4_out), .sel(shamt[0]));
  Multiplexer #(.enable("false")) multiplexer_5 (.in0(in[4]), .in1(in[5]), .out(multiplexer_5_out), .sel(shamt[0]));
  Multiplexer #(.enable("false")) multiplexer_6 (.in0(in[5]), .in1(in[6]), .out(multiplexer_6_out), .sel(shamt[0]));
  Multiplexer #(.enable("false")) multiplexer_7 (.in0(in[6]), .in1(in[7]), .out(multiplexer_7_out), .sel(shamt[0]));
  Multiplexer #(.enable("false")) multiplexer_8 (.in0(in[7]), .in1(in[8]), .out(multiplexer_8_out), .sel(shamt[0]));
  Multiplexer #(.enable("false")) multiplexer_9 (
    .in0(multiplexer_1_out), .in1(multiplexer_3_out), .out(multiplexer_9_out), .sel(shamt[1]));
  Multiplexer #(.enable("false")) multiplexer_10 (.in0(in[8]), .in1(in[9]), .out(multiplexer_10_out), .sel(shamt[0]));
  Multiplexer #(.enable("false")) multiplexer_11 (.in0(in[9]), .in1(in[10]), .out(multiplexer_11_out), .sel(shamt[0]));
  Multiplexer #(.enable("false")) multiplexer_12 (.in0(in[10]), .in1(in[11]), .out(multiplexer_12_out), .sel(shamt[0]));
  Multiplexer #(.enable("false")) multiplexer_13 (
    .in0(multiplexer_2_out), .in1(multiplexer_4_out), .out(multiplexer_13_out), .sel(shamt[1]));
  Multiplexer #(.enable("false")) multiplexer_14 (
    .in0(multiplexer_3_out), .in1(multiplexer_5_out), .out(multiplexer_14_out), .sel(shamt[1]));
  Multiplexer #(.enable("false")) multiplexer_15 (
    .in0(multiplexer_4_out), .in1(multiplexer_6_out), .out(multiplexer_15_out), .sel(shamt[1]));
  Multiplexer #(.enable("false")) multiplexer_16 (.in0(in[11]), .in1(in[12]), .out(multiplexer_16_out), .sel(shamt[0]));
  Multiplexer #(.enable("false")) multiplexer_17 (.in0(in[12]), .in1(in[13]), .out(multiplexer_17_out), .sel(shamt[0]));
  Multiplexer #(.enable("false")) multiplexer_18 (.in0(in[13]), .in1(in[14]), .out(multiplexer_18_out), .sel(shamt[0]));
  Multiplexer #(.enable("false")) multiplexer_19 (
    .in0(multiplexer_5_out), .in1(multiplexer_7_out), .out(multiplexer_19_out), .sel(shamt[1]));
  Multiplexer #(.enable("false")) multiplexer_20 (
    .in0(multiplexer_6_out), .in1(multiplexer_8_out), .out(multiplexer_20_out), .sel(shamt[1]));
  Multiplexer #(.enable("false")) multiplexer_21 (
    .in0(multiplexer_7_out), .in1(multiplexer_10_out), .out(multiplexer_21_out), .sel(shamt[1]));
  Multiplexer #(.enable("false")) multiplexer_22 (.in0(in[14]), .in1(in[15]), .out(multiplexer_22_out), .sel(shamt[0]));
  Multiplexer #(.enable("false")) multiplexer_23 (.in0(in[15]), .in1(1'b0), .out(multiplexer_23_out), .sel(shamt[0]));
  Multiplexer #(.enable("false")) multiplexer_24 (
    .in0(multiplexer_8_out), .in1(multiplexer_11_out), .out(multiplexer_24_out), .sel(shamt[1]));
  Multiplexer #(.enable("false")) multiplexer_25 (
    .in0(multiplexer_10_out), .in1(multiplexer_12_out), .out(multiplexer_25_out), .sel(shamt[1]));
  Multiplexer #(.enable("false")) multiplexer_26 (
    .in0(multiplexer_9_out), .in1(multiplexer_19_out), .out(out[0]), .sel(shamt[2]));
  Multiplexer #(.enable("false")) multiplexer_27 (
    .in0(multiplexer_11_out), .in1(multiplexer_16_out), .out(multiplexer_27_out), .sel(shamt[1]));
  Multiplexer #(.enable("false")) multiplexer_28 (
    .in0(multiplexer_12_out), .in1(multiplexer_17_out), .out(multiplexer_28_out), .sel(shamt[1]));
  Multiplexer #(.enable("false")) multiplexer_29 (
    .in0(multiplexer_16_out), .in1(multiplexer_18_out), .out(multiplexer_29_out), .sel(shamt[1]));
  Multiplexer #(.enable("false")) multiplexer_30 (
    .in0(multiplexer_13_out), .in1(multiplexer_20_out), .out(out[1]), .sel(shamt[2]));
  Multiplexer #(.enable("false")) multiplexer_31 (
    .in0(multiplexer_14_out), .in1(multiplexer_21_out), .out(out[2]), .sel(shamt[2]));
  Multiplexer #(.enable("false")) multiplexer_32 (
    .in0(multiplexer_17_out), .in1(multiplexer_22_out), .out(multiplexer_32_out), .sel(shamt[1]));
  Multiplexer #(.enable("false")) multiplexer_33 (
    .in0(multiplexer_18_out), .in1(multiplexer_23_out), .out(multiplexer_33_out), .sel(shamt[1]));
  Multiplexer #(.enable("false")) multiplexer_34 (
    .in0(multiplexer_22_out), .in1(1'b0), .out(multiplexer_34_out), .sel(shamt[1]));
  Multiplexer #(.enable("false")) multiplexer_35 (
    .in0(multiplexer_15_out), .in1(multiplexer_24_out), .out(out[3]), .sel(shamt[2]));
  Multiplexer #(.enable("false")) multiplexer_36 (
    .in0(multiplexer_19_out), .in1(multiplexer_25_out), .out(out[4]), .sel(shamt[2]));
  Multiplexer #(.enable("false")) multiplexer_37 (
    .in0(multiplexer_20_out), .in1(multiplexer_27_out), .out(out[5]), .sel(shamt[2]));
  Multiplexer #(.enable("false")) multiplexer_38 (
    .in0(multiplexer_23_out), .in1(1'b0), .out(multiplexer_38_out), .sel(shamt[1]));
  Multiplexer #(.enable("false")) multiplexer_39 (
    .in0(multiplexer_21_out), .in1(multiplexer_28_out), .out(out[6]), .sel(shamt[2]));
  Multiplexer #(.enable("false")) multiplexer_40 (
    .in0(multiplexer_24_out), .in1(multiplexer_29_out), .out(out[7]), .sel(shamt[2]));
  Multiplexer #(.enable("false")) multiplexer_41 (
    .in0(multiplexer_25_out), .in1(multiplexer_32_out), .out(out[8]), .sel(shamt[2]));
  Multiplexer #(.enable("false")) multiplexer_42 (
    .in0(multiplexer_27_out), .in1(multiplexer_33_out), .out(out[9]), .sel(shamt[2]));
  Multiplexer #(.enable("false")) multiplexer_43 (
    .in0(multiplexer_28_out), .in1(multiplexer_34_out), .out(out[10]), .sel(shamt[2]));
  Multiplexer #(.enable("false")) multiplexer_44 (
    .in0(multiplexer_29_out), .in1(multiplexer_38_out), .out(out[11]), .sel(shamt[2]));
  Multiplexer #(.enable("false")) multiplexer_45 (.in0(multiplexer_32_out), .in1(1'b0), .out(out[12]), .sel(shamt[2]));
  Multiplexer #(.enable("false")) multiplexer_46 (.in0(multiplexer_33_out), .in1(1'b0), .out(out[13]), .sel(shamt[2]));
  Multiplexer #(.enable("false")) multiplexer_47 (.in0(multiplexer_34_out), .in1(1'b0), .out(out[14]), .sel(shamt[2]));
  Multiplexer #(.enable("false")) multiplexer_48 (.in0(multiplexer_38_out), .in1(1'b0), .out(out[15]), .sel(shamt[2]));
endmodule

module control (
  input  [15:0] instruction,
  output [11:0] addr,
  output [5:0] immed,
  output [2:0] shamt,
  output [2:0] Rd,
  output [2:0] Rt,
  output [2:0] Rs,
  output Rd_is_Rt,
  output shift,
  output shift_right,
  output load,
  output store,
  output bne,
  output blt,
  output \input ,
  output \output ,
  output write_en,
  output ALU_immed,
  output [1:0] jump,
  output [1:0] ALU_op
);

  wire and_1_out, and_2_out, and_3_out, and_4_out, and_5_out, and_6_out, and_7_out, and_8_out, and_9_out,
       and_10_out, and_11_out, and_12_out, and_13_out, and_14_out, not_1_out, xor_1_out, xor_2_out, xor_3_out;

  and and_1 (and_1_out, ~instruction[15], ~instruction[14], ~instruction[13], instruction[12]);  // AND_Gate
  and and_2 (and_2_out, ~instruction[15], instruction[14], instruction[13], instruction[12]);  // AND_Gate
  or or_1 (Rd_is_Rt, and_1_out, and_2_out, and_3_out);
  and and_3 (and_3_out, instruction[15], instruction[14], instruction[13], ~instruction[12]);  // AND_Gate
  and and_4 (and_4_out, ~instruction[15], ~instruction[14], instruction[13], instruction[12]);  // AND_Gate
  and and_5 (and_5_out, ~instruction[15], instruction[14], ~instruction[13], ~instruction[12]);  // AND_Gate
  or or_2 (ALU_op[1], and_4_out, and_5_out, and_6_out);
  and and_6 (and_6_out, instruction[15], ~instruction[14], ~instruction[13], instruction[12]);  // AND_Gate
  and and_7 (and_7_out, ~instruction[15], ~instruction[14], instruction[13], ~instruction[12]);  // AND_Gate
  and and_8 (and_8_out, ~instruction[15], instruction[14], ~instruction[13], ~instruction[12]);  // AND_Gate
  or or_3 (ALU_op[0], and_7_out, and_8_out, and_9_out, and_10_out);
  and and_9 (and_9_out, instruction[15], ~instruction[14], ~instruction[13], instruction[12]);  // AND_Gate
  and and_10 (and_10_out, instruction[15], ~instruction[14], instruction[13], ~instruction[12]);  // AND_Gate
  not not_1 (not_1_out, instruction[15]);
  and and_11 (and_11_out, instruction[15], instruction[14], xor_1_out);
  or or_4 (write_en, not_1_out, and_11_out);
  xor xor_1 (xor_1_out, instruction[13], instruction[12]);
  and and_12 (and_12_out, ~instruction[15], ~instruction[14], ~instruction[13], instruction[12]);  // AND_Gate
  and and_13 (and_13_out, ~instruction[15], instruction[14], instruction[13], instruction[12]);  // AND_Gate
  or or_5 (ALU_immed, and_12_out, and_13_out, and_14_out);
  and and_14 (and_14_out, instruction[15], ~instruction[14], ~instruction[13], ~instruction[12]);  // AND_Gate
  xor xor_2 (xor_2_out, instruction[13], instruction[12]);
  and and_15 (shift, ~instruction[15], instruction[14], xor_2_out);  // AND_Gate
  not not_2 (shift_right, instruction[12]);
  and and_16 (load, ~instruction[15], instruction[14], instruction[13], instruction[12]);  // AND_Gate
  and and_17 (store, instruction[15], ~instruction[14], ~instruction[13], ~instruction[12]);  // AND_Gate
  and and_18 (bne, instruction[15], ~instruction[14], ~instruction[13], instruction[12]);  // AND_Gate
  and and_19 (blt, instruction[15], ~instruction[14], instruction[13], ~instruction[12]);  // AND_Gate
  and and_20 (jump[1], instruction[15], instruction[14], ~instruction[13]);  // AND_Gate
  xor xor_3 (xor_3_out, instruction[14], instruction[13]);
  and and_21 (jump[0], instruction[15], xor_3_out, instruction[12]);
  and and_22 (\input , instruction[15], instruction[14], instruction[13], ~instruction[12]);  // AND_Gate
  and and_23 (\output , instruction[15], instruction[14], instruction[13], instruction[12]);

  assign addr = instruction[11:0];
  assign immed = instruction[5:0];
  assign Rd = instruction[5:3];
  assign Rs = instruction[11:9];
  assign Rt = instruction[8:6];
  assign shamt = instruction[2:0];

  // Other names for the same wires on the sheet: opcode[3:0] = instruction[15:12]
endmodule
